// Logisim project F.6.circ as structural Verilog: 4 circuits, main circuit main
module main (
);

  wire add_en, clk, jalr_en, not_2_out, op_en, or_1_out, PcAllign, por_1_out, w_en;
  wire [1:0] op_sel, w_sel;
  wire [4:0] add_rd, add_rs, jalr_rd, jalr_rs, rs0, w_addr;
  wire [7:0] InsAddr;
  wire [31:0] add_rdd, adder_1_out, gpr_1_rdata0, gpr_1_x0, gpr_1_x1, gpr_1_x10, IR, jalr_pc, jalr_rdd,
       NextPc, PC, rom_1_data, w_data;

  Clock u_clk (.out(clk));
  Adder #(.width(32)) adder_1 (.a({PC[31:10], InsAddr, PC[1:0]}), .b(32'h4), .out(adder_1_out));  // open: cin, cout
  Register #(.width(32)) register_1 (.D(adder_1_out), .en(PcAllign), .clk(clk), .Q(NextPc), .clr(por_1_out));
  POR por_1 (.out(por_1_out));
  or or_1 (or_1_out, PC[0], PC[1]);
  // Probe on {PC[31:10], InsAddr, PC[1:0]}
  Multiplexer #(.width(32)) multiplexer_1 (
    .in0(NextPc), .in1(jalr_pc), .out({PC[31:10], InsAddr, PC[1:0]}), .sel(jalr_en));
  not not_1 (PcAllign, or_1_out);
  LED led_1 (.in(or_1_out));
  // Probe on w_data
  // Probe on w_addr
  // Probe on rs0
  ROM #(.dataWidth(32)) rom_1 (.addr(InsAddr), .data(rom_1_data));
  not not_2 (not_2_out, clk);
  GPR gpr_1 (
    .clk(not_2_out), .wdata(w_data), .waddr(w_addr), .wen(w_en), .raddr0(rs0), .x0(gpr_1_x0), .x1(gpr_1_x1),
    .x10(gpr_1_x10), .rdata0(gpr_1_rdata0));  // open: radd1, rdata1
  Register #(.width(32)) register_2 (.D(rom_1_data), .en(1'b1), .clk(clk), .Q(IR));  // open: clr
  // Probe on gpr_1_x0
  // Probe on gpr_1_x1
  // Probe on gpr_1_x10
  // Probe on IR
  // Probe on gpr_1_rdata0
  // Probe on jalr_rs
  // Probe on add_rs
  // Probe on add_rd
  jalr jalr_1 (
    .OpCode(IR), .APC(NextPc), .Rsd(gpr_1_rdata0), .is_jalr(jalr_en), .rd(jalr_rd), .rs(jalr_rs),
    .Rdd(jalr_rdd), .NextPc(jalr_pc));
  addi addi_1 (.OpCode(IR), .rsd(gpr_1_rdata0), .is_addi(add_en), .rd(add_rd), .rs(add_rs), .Rdd(add_rdd));
  Priority_Encoder #(.select(2)) priority_encoder_1 (
    .in0(add_en), .in1(jalr_en), .out(w_sel), .gs(w_en));  // open: in2, in3, en_out, en_in
  // Probe on op_sel
  Priority_Encoder #(.select(2)) priority_encoder_2 (
    .in0(add_en), .in1(jalr_en), .out(op_sel), .gs(op_en));  // open: in2, in3, en_out, en_in
  Multiplexer #(.enable("true"), .select(2), .width(32)) multiplexer_2 (
    .in0(add_rdd), .in1(jalr_rdd), .out(w_data), .sel(w_sel), .en(w_en));  // open: in2, in3
  Multiplexer #(.enable("true"), .select(2), .width(5)) multiplexer_3 (
    .in0(add_rd), .in1(jalr_rd), .out(w_addr), .sel(w_sel), .en(w_en));  // open: in2, in3
  Multiplexer #(.enable("true"), .select(2), .width(5)) multiplexer_4 (
    .in0(add_rs), .in1(jalr_rs), .out(rs0), .sel(op_sel), .en(op_en));  // open: in2, in3
  // Probe on add_rdd

  // Other names for the same wires on the sheet: PC[9:2] = InsAddr

  // Notes on the sheet:
  //   contents of rom_1 (hex, n*v repeats v):
  //   ff700513 10000e7 c000e7 c00067 a50513 8067
endmodule

module GPR (
  input  clk,
  input  [31:0] wdata,
  input  [4:0] waddr,
  input  wen,
  input  [4:0] raddr0,
  input  [4:0] radd1,
  output [31:0] x0,
  output [31:0] x1,
  output [31:0] x10,
  output [31:0] rdata0,
  output [31:0] rdata1
);

  wire decoder_1_out0, decoder_1_out1, decoder_1_out2, decoder_1_out3, decoder_1_out4, decoder_1_out5,
       decoder_1_out6, decoder_1_out7, decoder_1_out8, decoder_1_out9, decoder_1_out10, decoder_1_out11,
       decoder_1_out12, decoder_1_out13, decoder_1_out14, decoder_1_out15, decoder_1_out16, decoder_1_out17,
       decoder_1_out18, decoder_1_out19, decoder_1_out20, decoder_1_out21, decoder_1_out22, decoder_1_out23,
       decoder_1_out24, decoder_1_out25, decoder_1_out26, decoder_1_out27, decoder_1_out28, decoder_1_out29,
       decoder_1_out30, decoder_1_out31;
  wire [31:0] register_2_q, register_3_q, register_4_q, register_6_q, register_7_q, register_8_q,
       register_9_q, register_11_q, register_12_q, register_13_q, register_14_q, register_15_q,
       register_16_q, register_17_q, register_18_q, register_19_q, register_20_q, register_21_q,
       register_22_q, register_23_q, register_24_q, register_25_q, register_26_q, register_27_q,
       register_28_q, register_29_q, register_30_q, register_31_q, register_32_q;

  Decoder #(.select(5)) decoder_1 (
    .out0(decoder_1_out0), .out1(decoder_1_out1), .out2(decoder_1_out2), .out3(decoder_1_out3),
    .out4(decoder_1_out4), .out5(decoder_1_out5), .out6(decoder_1_out6), .out7(decoder_1_out7),
    .out8(decoder_1_out8), .out9(decoder_1_out9), .out10(decoder_1_out10), .out11(decoder_1_out11),
    .out12(decoder_1_out12), .out13(decoder_1_out13), .out14(decoder_1_out14), .out15(decoder_1_out15),
    .out16(decoder_1_out16), .out17(decoder_1_out17), .out18(decoder_1_out18), .out19(decoder_1_out19),
    .out20(decoder_1_out20), .out21(decoder_1_out21), .out22(decoder_1_out22), .out23(decoder_1_out23),
    .out24(decoder_1_out24), .out25(decoder_1_out25), .out26(decoder_1_out26), .out27(decoder_1_out27),
    .out28(decoder_1_out28), .out29(decoder_1_out29), .out30(decoder_1_out30), .out31(decoder_1_out31),
    .sel(waddr), .en(wen));
  Register #(.width(32)) register_1 (.D({32{1'b0}}), .en(decoder_1_out0), .clk(clk), .Q(x0));  // open: clr
  Register #(.width(32)) register_2 (.D(wdata), .en(decoder_1_out8), .clk(clk), .Q(register_2_q));  // open: clr
  Register #(.width(32)) register_3 (.D(wdata), .en(decoder_1_out16), .clk(clk), .Q(register_3_q));  // open: clr
  Register #(.width(32)) register_4 (.D(wdata), .en(decoder_1_out24), .clk(clk), .Q(register_4_q));  // open: clr
  Register #(.width(32)) register_5 (.D(wdata), .en(decoder_1_out1), .clk(clk), .Q(x1));  // open: clr
  Register #(.width(32)) register_6 (.D(wdata), .en(decoder_1_out9), .clk(clk), .Q(register_6_q));  // open: clr
  Register #(.width(32)) register_7 (.D(wdata), .en(decoder_1_out17), .clk(clk), .Q(register_7_q));  // open: clr
  Register #(.width(32)) register_8 (.D(wdata), .en(decoder_1_out25), .clk(clk), .Q(register_8_q));  // open: clr
  Register #(.width(32)) register_9 (.D(wdata), .en(decoder_1_out2), .clk(clk), .Q(register_9_q));  // open: clr
  Register #(.width(32)) register_10 (.D(wdata), .en(decoder_1_out10), .clk(clk), .Q(x10));  // open: clr
  Register #(.width(32)) register_11 (.D(wdata), .en(decoder_1_out18), .clk(clk), .Q(register_11_q));  // open: clr
  Register #(.width(32)) register_12 (.D(wdata), .en(decoder_1_out26), .clk(clk), .Q(register_12_q));  // open: clr
  Register #(.width(32)) register_13 (.D(wdata), .en(decoder_1_out3), .clk(clk), .Q(register_13_q));  // open: clr
  Register #(.width(32)) register_14 (.D(wdata), .en(decoder_1_out11), .clk(clk), .Q(register_14_q));  // open: clr
  Register #(.width(32)) register_15 (.D(wdata), .en(decoder_1_out19), .clk(clk), .Q(register_15_q));  // open: clr
  Register #(.width(32)) register_16 (.D(wdata), .en(decoder_1_out27), .clk(clk), .Q(register_16_q));  // open: clr
  Register #(.width(32)) register_17 (.D(wdata), .en(decoder_1_out4), .clk(clk), .Q(register_17_q));  // open: clr
  Register #(.width(32)) register_18 (.D(wdata), .en(decoder_1_out12), .clk(clk), .Q(register_18_q));  // open: clr
  Register #(.width(32)) register_19 (.D(wdata), .en(decoder_1_out20), .clk(clk), .Q(register_19_q));  // open: clr
  Register #(.width(32)) register_20 (.D(wdata), .en(decoder_1_out28), .clk(clk), .Q(register_20_q));  // open: clr
  Register #(.width(32)) register_21 (.D(wdata), .en(decoder_1_out5), .clk(clk), .Q(register_21_q));  // open: clr
  Register #(.width(32)) register_22 (.D(wdata), .en(decoder_1_out13), .clk(clk), .Q(register_22_q));  // open: clr
  Register #(.width(32)) register_23 (.D(wdata), .en(decoder_1_out21), .clk(clk), .Q(register_23_q));  // open: clr
  Register #(.width(32)) register_24 (.D(wdata), .en(decoder_1_out29), .clk(clk), .Q(register_24_q));  // open: clr
  Register #(.width(32)) register_25 (.D(wdata), .en(decoder_1_out6), .clk(clk), .Q(register_25_q));  // open: clr
  Register #(.width(32)) register_26 (.D(wdata), .en(decoder_1_out14), .clk(clk), .Q(register_26_q));  // open: clr
  Register #(.width(32)) register_27 (.D(wdata), .en(decoder_1_out22), .clk(clk), .Q(register_27_q));  // open: clr
  Register #(.width(32)) register_28 (.D(wdata), .en(decoder_1_out30), .clk(clk), .Q(register_28_q));  // open: clr
  Register #(.width(32)) register_29 (.D(wdata), .en(decoder_1_out7), .clk(clk), .Q(register_29_q));  // open: clr
  Register #(.width(32)) register_30 (.D(wdata), .en(decoder_1_out15), .clk(clk), .Q(register_30_q));  // open: clr
  Register #(.width(32)) register_31 (.D(wdata), .en(decoder_1_out23), .clk(clk), .Q(register_31_q));  // open: clr
  Register #(.width(32)) register_32 (.D(wdata), .en(decoder_1_out31), .clk(clk), .Q(register_32_q));  // open: clr
  Multiplexer #(.select(5), .width(32)) multiplexer_1 (
    .in0(x0), .in1(x1), .in2(register_9_q), .in3(register_13_q), .in4(register_17_q), .in5(register_21_q),
    .in6(register_25_q), .in7(register_29_q), .in8(register_2_q), .in9(register_6_q), .in10(x10),
    .in11(register_14_q), .in12(register_18_q), .in13(register_22_q), .in14(register_26_q),
    .in15(register_30_q), .in16(register_3_q), .in17(register_7_q), .in18(register_11_q),
    .in19(register_15_q), .in20(register_19_q), .in21(register_23_q), .in22(register_27_q),
    .in23(register_31_q), .in24(register_4_q), .in25(register_8_q), .in26(register_12_q),
    .in27(register_16_q), .in28(register_20_q), .in29(register_24_q), .in30(register_28_q),
    .in31(register_32_q), .out(rdata0), .sel(raddr0));
  Multiplexer #(.select(5), .width(32)) multiplexer_2 (
    .in0(x0), .in1(x1), .in2(register_9_q), .in3(register_13_q), .in4(register_17_q), .in5(register_21_q),
    .in6(register_25_q), .in7(register_29_q), .in8(register_2_q), .in9(register_6_q), .in10(x10),
    .in11(register_14_q), .in12(register_18_q), .in13(register_22_q), .in14(register_26_q),
    .in15(register_30_q), .in16(register_3_q), .in17(register_7_q), .in18(register_11_q),
    .in19(register_15_q), .in20(register_19_q), .in21(register_23_q), .in22(register_27_q),
    .in23(register_31_q), .in24(register_4_q), .in25(register_8_q), .in26(register_12_q),
    .in27(register_16_q), .in28(register_20_q), .in29(register_24_q), .in30(register_28_q),
    .in31(register_32_q), .out(rdata1), .sel(radd1));
endmodule

module addi (
  input  [31:0] OpCode,
  input  [31:0] rsd,
  output is_addi,
  output [4:0] rd,
  output [4:0] rs,
  output [31:0] Rdd
);

  wire comparator_1_eq, comparator_2_eq;
  wire [31:0] imm;

  assign imm = {{20{OpCode[31]}}, OpCode[31:20]};  // Bit_Extender bit_extender_1
  // Probe on imm
  Comparator #(.width(7)) comparator_1 (.a(OpCode[6:0]), .b(7'b0010011), .eq(comparator_1_eq));  // open: gt, lt
  Comparator #(.width(3)) comparator_2 (.a(OpCode[14:12]), .b(3'b000), .eq(comparator_2_eq));  // open: gt, lt
  Adder #(.width(32)) adder_1 (.a(imm), .b(rsd), .out(Rdd));  // open: cin, cout
  and and_1 (is_addi, comparator_1_eq, comparator_2_eq);

  assign rd = OpCode[11:7];
  assign rs = OpCode[19:15];

  // Notes on the sheet:
  //   OpCode: initial=0x1400513
endmodule

module jalr (
  input  [31:0] OpCode,
  input  [31:0] APC,
  input  [31:0] Rsd,
  output is_jalr,
  output [4:0] rd,
  output [4:0] rs,
  output [31:0] Rdd,
  output [31:0] NextPc
);

  wire comparator_1_eq, comparator_2_eq;
  wire [31:0] bit_extender_1_out, imm;

  assign bit_extender_1_out = {{20{OpCode[31]}}, OpCode[31:20]};  // Bit_Extender bit_extender_1
  Adder #(.width(32)) adder_1 (.a(imm), .b(Rsd), .out(NextPc));  // open: cin, cout
  Comparator #(.width(7)) comparator_1 (.a(OpCode[6:0]), .b(7'b1100111), .eq(comparator_1_eq));  // open: gt, lt
  Comparator #(.width(3)) comparator_2 (.a(OpCode[14:12]), .b(3'b000), .eq(comparator_2_eq));  // open: gt, lt
  assign imm = bit_extender_1_out & 32'hfffffffe;  // AND_Gate and_1, 32 bits wide
  and and_2 (is_jalr, comparator_1_eq, comparator_2_eq);

  assign rd = OpCode[11:7];
  assign Rdd = APC;
  assign rs = OpCode[19:15];
endmodule
