// Logisim project F3.combine.circ as structural Verilog: 23 circuits, main circuit main
module main (
  output [3:0] out_1
);

  wire a, b, c, d, e, f, full_sub_4_1_bout, g, h, not_1_out, twoscomplement_1_overflow;
  wire [3:0] dipswitch_1_sw4, dipswitch_2_sw4, twoscomplement_1_s;
  wire [7:0] sevenseghex_2_out_3;

  DipSwitch #(.number(4)) dipswitch_1 (
    .sw1(dipswitch_1_sw4[3]), .sw2(dipswitch_1_sw4[2]), .sw3(dipswitch_1_sw4[1]), .sw4(dipswitch_1_sw4[0]));
  DipSwitch #(.number(4)) dipswitch_2 (
    .sw1(dipswitch_2_sw4[3]), .sw2(dipswitch_2_sw4[2]), .sw3(dipswitch_2_sw4[1]), .sw4(dipswitch_2_sw4[0]));
  full_sub_4 full_sub_4_1 (.Bin(1'b0), .A1(dipswitch_1_sw4), .A0(dipswitch_2_sw4), .D(out_1), .Bout(full_sub_4_1_bout));
  twoscomplement twoscomplement_1 (
    .A(dipswitch_1_sw4), .B(dipswitch_2_sw4), .S(twoscomplement_1_s), .overflow(twoscomplement_1_overflow));  // open: Cin, Cout
  not not_1 (not_1_out, 1'b0);
  LED led_1 (.in(full_sub_4_1_bout));
  _7_Segment_Display u_7_segment_display_1 (.g(g), .f(f), .a(a), .b(b), .e(e), .d(d), .c(c), .dp(h));
  sevenSegHex sevenseghex_1 (.in_1(out_1), .hex_enable(not_1_out), .out_3({h, g, f, e, d, c, b, a}));
  sevenSegHex sevenseghex_2 (.in_1({1'b0, twoscomplement_1_s[2:0]}), .out_3(sevenseghex_2_out_3));  // open: hex_enable
  _7_Segment_Display u_7_segment_display_2 (.g(twoscomplement_1_s[3]));  // open: f, a, b, e, d, c, dp
  _7_Segment_Display u_7_segment_display_3 (
    .g(sevenseghex_2_out_3[6]), .f(sevenseghex_2_out_3[5]), .a(sevenseghex_2_out_3[0]),
    .b(sevenseghex_2_out_3[1]), .e(sevenseghex_2_out_3[4]), .d(sevenseghex_2_out_3[3]),
    .c(sevenseghex_2_out_3[2]), .dp(sevenseghex_2_out_3[7]));
  LED led_2 (.in(twoscomplement_1_overflow));
endmodule

module tfd (
  input  EN,
  input  A1,
  input  A0,
  output Y3,
  output Y2,
  output Y1,
  output Y0
);

  wire not_1_out, not_2_out;

  not not_1 (not_1_out, A1);
  not not_2 (not_2_out, A0);
  and and_1 (Y3, A1, EN, A0);
  and and_2 (Y2, A1, EN, not_2_out);
  and and_3 (Y1, not_1_out, EN, A0);
  and and_4 (Y0, not_1_out, EN, not_2_out);
endmodule

module ted (
  input  EN,
  input  A2,
  input  A1,
  input  A0,
  output Y7,
  output Y6,
  output Y5,
  output Y4,
  output Y3,
  output Y2,
  output Y1,
  output Y0
);

  wire and_1_out, and_2_out;

  and and_1 (and_1_out, EN, A2);
  and and_2 (and_2_out, EN, ~A2);  // AND_Gate
  tfd tfd_1 (.EN(and_1_out), .A1(A1), .A0(A0), .Y3(Y7), .Y2(Y6), .Y1(Y5), .Y0(Y4));
  tfd tfd_2 (.EN(and_2_out), .A1(A1), .A0(A0), .Y3(Y3), .Y2(Y2), .Y1(Y1), .Y0(Y0));
endmodule

module digtSeven (
  input  [3:0] in_1
);

  wire a, b, c, d, e, f, g, h, n0, n1, n2, n3, n4, n5, n6, n7, n8, n9, n10, n11, n12, n13, n14, n15,
       not_1_out;

  not not_1 (not_1_out, in_1[3]);
  _7_Segment_Display u_7_segment_display_1 (.g(g), .f(f), .a(a), .b(b), .e(e), .d(d), .c(c), .dp(h));
  ted ted_1 (
    .EN(in_1[3]), .A2(in_1[2]), .A1(in_1[1]), .A0(in_1[0]), .Y7(n15), .Y6(n14), .Y5(n13), .Y4(n12), .Y3(n11),
    .Y2(n10), .Y1(n9), .Y0(n8));
  ted ted_2 (
    .EN(not_1_out), .A2(in_1[2]), .A1(in_1[1]), .A0(in_1[0]), .Y7(n7), .Y6(n6), .Y5(n5), .Y4(n4), .Y3(n3),
    .Y2(n2), .Y1(n1), .Y0(n0));
  or or_1 (a, n0, n2, n3, n5, n6, n7, n8, n9, n9);
  or or_2 (b, n0, n1, n2, n3, n4, n7, n8, n9, n9);
  or or_3 (c, n0, n1, n3, n4, n5, n6, n7, n8, n9);
  or or_4 (d, n0, n2, n3, n5, n5, n6, n8, n8, n9);
  or or_5 (e, n0, n2, n6, n8, n8, n8, n8, n8, n8);
  or or_6 (f, n0, n4, n5, n6, n8, n9, n9, n9, n9);
  or or_7 (g, n2, n2, n3, n4, n5, n6, n6, n8, n9);
  nor nor_1 (h, n2, n0, n1, n3, n4, n6, n7, n8, n9, n5);
endmodule

module sevenSegHex (
  input  [3:0] in_1,
  input  hex_enable,
  output [7:0] out_3
);

  wire ap, bp, cp, dp, ep, fp, gp, hp, n0, n1, n2, n3, n4, n5, n6, n7, n8, n9, n10, n11, n12, n13, n14, n15,
       not_1_out, or_1_out, or_2_out, or_3_out, or_4_out, or_5_out, or_6_out, or_7_out;

  not not_1 (not_1_out, in_1[3]);
  or or_1 (or_1_out, gp, n15, n10, n13, n11, n14, n14);
  _7_Segment_Display u_7_segment_display_1 (
    .g(out_3[6]), .f(out_3[5]), .a(out_3[0]), .b(out_3[1]), .e(out_3[4]), .d(out_3[3]), .c(out_3[2]),
    .dp(out_3[7]));
  or or_2 (or_2_out, ap, ap, n10, n12, n12, n14, n15);
  or or_3 (or_3_out, bp, bp, n13, n13, n13, n10, n10);
  or or_4 (or_4_out, cp, cp, n10, n11, n11, n13, n13);
  or or_5 (or_5_out, dp, dp, n12, n11, n11, n13, n14);
  or or_6 (or_6_out, ep, n15, n12, n10, n11, n13, n14);
  or or_7 (or_7_out, fp, n15, n12, n10, n11, n14, n14);
  and and_1 (out_3[7], ~hex_enable, hp);  // AND_Gate
  ted ted_1 (
    .EN(in_1[3]), .A2(in_1[2]), .A1(in_1[1]), .A0(in_1[0]), .Y7(n15), .Y6(n14), .Y5(n13), .Y4(n12), .Y3(n11),
    .Y2(n10), .Y1(n9), .Y0(n8));
  ted ted_2 (
    .EN(not_1_out), .A2(in_1[2]), .A1(in_1[1]), .A0(in_1[0]), .Y7(n7), .Y6(n6), .Y5(n5), .Y4(n4), .Y3(n3),
    .Y2(n2), .Y1(n1), .Y0(n0));
  and and_2 (out_3[0], ~out_3[7], or_2_out);  // AND_Gate
  and and_3 (out_3[1], ~out_3[7], or_3_out);  // AND_Gate
  and and_4 (out_3[2], ~out_3[7], or_4_out);  // AND_Gate
  and and_5 (out_3[3], ~out_3[7], or_5_out);  // AND_Gate
  and and_6 (out_3[4], ~out_3[7], or_6_out);  // AND_Gate
  and and_7 (out_3[5], ~out_3[7], or_7_out);  // AND_Gate
  and and_8 (out_3[6], ~out_3[7], or_1_out);  // AND_Gate
  or or_8 (ap, n0, n2, n3, n5, n6, n7, n8, n9, n9);
  or or_9 (bp, n0, n1, n2, n3, n4, n7, n8, n9, n9);
  or or_10 (cp, n0, n1, n3, n4, n5, n6, n7, n8, n9);
  or or_11 (dp, n0, n2, n3, n5, n5, n6, n8, n8, n9);
  or or_12 (ep, n0, n2, n6, n8, n8, n8, n8, n8, n8);
  or or_13 (fp, n0, n4, n5, n6, n8, n9, n9, n9, n9);
  or or_14 (gp, n2, n2, n3, n4, n5, n6, n6, n8, n9);
  nor nor_1 (hp, n2, n0, n1, n3, n4, n6, n7, n8, n9, n5);

  // Other names for the same wires on the sheet: a = out_3[0]; b = out_3[1]; c = out_3[2]; d = out_3[3]; e = out_3[4];
  //   f = out_3[5]; g = out_3[6]; h = out_3[7]

  // Notes on the sheet:
  //   hex extension
endmodule

module fourSixteenEncoder (
);

  wire dipswitch_1_sw2, dipswitch_1_sw3, dipswitch_1_sw4, dipswitch_1_sw5, dipswitch_1_sw6, dipswitch_1_sw7,
       dipswitch_1_sw8, dipswitch_1_sw9, dipswitch_1_sw10, dipswitch_1_sw11, dipswitch_1_sw12,
       dipswitch_1_sw13, dipswitch_1_sw14, dipswitch_1_sw15, dipswitch_1_sw16, y0, y1, y2, y3;
  wire [7:0] sevenseghex_1_out_3;

  DipSwitch #(.number(16)) dipswitch_1 (
    .sw2(dipswitch_1_sw2), .sw3(dipswitch_1_sw3), .sw4(dipswitch_1_sw4), .sw5(dipswitch_1_sw5),
    .sw6(dipswitch_1_sw6), .sw7(dipswitch_1_sw7), .sw8(dipswitch_1_sw8), .sw9(dipswitch_1_sw9),
    .sw10(dipswitch_1_sw10), .sw11(dipswitch_1_sw11), .sw12(dipswitch_1_sw12), .sw13(dipswitch_1_sw13),
    .sw14(dipswitch_1_sw14), .sw15(dipswitch_1_sw15), .sw16(dipswitch_1_sw16));  // open: sw1
  or or_1 (y0, dipswitch_1_sw2, dipswitch_1_sw4, dipswitch_1_sw6, dipswitch_1_sw8, dipswitch_1_sw10, dipswitch_1_sw12, dipswitch_1_sw14, dipswitch_1_sw16);
  or or_2 (y1, dipswitch_1_sw3, dipswitch_1_sw4, dipswitch_1_sw7, dipswitch_1_sw8, dipswitch_1_sw11, dipswitch_1_sw12, dipswitch_1_sw15, dipswitch_1_sw16);
  or or_3 (y2, dipswitch_1_sw5, dipswitch_1_sw6, dipswitch_1_sw7, dipswitch_1_sw8, dipswitch_1_sw13, dipswitch_1_sw14, dipswitch_1_sw15, dipswitch_1_sw16);
  or or_4 (y3, dipswitch_1_sw9, dipswitch_1_sw10, dipswitch_1_sw11, dipswitch_1_sw12, dipswitch_1_sw13, dipswitch_1_sw14, dipswitch_1_sw15, dipswitch_1_sw16);
  sevenSegHex sevenseghex_1 (.in_1({y3, y2, y1, y0}), .hex_enable(1'b1), .out_3(sevenseghex_1_out_3));
  _7_Segment_Display u_7_segment_display_1 (
    .g(sevenseghex_1_out_3[6]), .f(sevenseghex_1_out_3[5]), .a(sevenseghex_1_out_3[0]),
    .b(sevenseghex_1_out_3[1]), .e(sevenseghex_1_out_3[4]), .d(sevenseghex_1_out_3[3]),
    .c(sevenseghex_1_out_3[2]), .dp(sevenseghex_1_out_3[7]));

  // Notes on the sheet:
  //   4-16 encoder
endmodule

module OneB_1of2 (
  input  d0,
  input  s,
  input  d1,
  output y
);

  wire and_1_out, and_2_out;

  and and_1 (and_1_out, d0, ~s);  // AND_Gate
  and and_2 (and_2_out, s, d1);
  or or_1 (y, and_1_out, and_2_out);
endmodule

module ThreeB_1of4 (
  input  [2:0] d3,
  input  [2:0] d2,
  input  s1,
  input  s0,
  input  [2:0] d0,
  input  [2:0] d1,
  output [2:0] out_7
);

  wire and_1_out, and_2_out, and_3_out, and_4_out, and_5_out, and_6_out, and_7_out, and_8_out, and_9_out,
       and_10_out, and_11_out, and_12_out, tfd_1_y0, tfd_1_y1, tfd_1_y2, tfd_1_y3;

  and and_1 (and_1_out, tfd_1_y3, d3[0]);
  and and_2 (and_2_out, tfd_1_y2, d2[0]);
  and and_3 (and_3_out, tfd_1_y0, d0[0]);
  and and_4 (and_4_out, tfd_1_y1, d1[0]);
  and and_5 (and_5_out, tfd_1_y3, d3[1]);
  and and_6 (and_6_out, tfd_1_y2, d2[1]);
  and and_7 (and_7_out, tfd_1_y0, d0[1]);
  and and_8 (and_8_out, tfd_1_y1, d1[1]);
  and and_9 (and_9_out, tfd_1_y3, d3[2]);
  and and_10 (and_10_out, tfd_1_y2, d2[2]);
  tfd tfd_1 (.EN(1'b1), .A1(s1), .A0(s0), .Y3(tfd_1_y3), .Y2(tfd_1_y2), .Y1(tfd_1_y1), .Y0(tfd_1_y0));
  and and_11 (and_11_out, tfd_1_y0, d0[2]);
  and and_12 (and_12_out, tfd_1_y1, d1[2]);
  or or_1 (out_7[0], and_3_out, and_4_out, and_2_out, and_1_out);
  or or_2 (out_7[1], and_7_out, and_8_out, and_6_out, and_5_out);
  or or_3 (out_7[2], and_11_out, and_12_out, and_10_out, and_9_out);
endmodule

module c4 (
  input  [3:0] n1,
  input  [3:0] n2,
  output equal
);

  wire xnor_1_out, xnor_2_out, xnor_3_out, xnor_4_out;

  xnor xnor_1 (xnor_1_out, n1[0], n2[0]);
  xnor xnor_2 (xnor_2_out, n1[1], n2[1]);
  xnor xnor_3 (xnor_3_out, n1[2], n2[2]);
  xnor xnor_4 (xnor_4_out, n1[3], n2[3]);
  and and_1 (equal, xnor_1_out, xnor_2_out, xnor_3_out, xnor_4_out);
  LED led_1 (.in(equal));
endmodule

module full_add_1 (
  input  Cin,
  input  A,
  input  B,
  output S,
  output Cout
);

  wire and_1_out, and_2_out, and_3_out, xor_1_out;

  and and_1 (and_1_out, Cin, A);
  and and_2 (and_2_out, Cin, B);
  and and_3 (and_3_out, A, B);
  xor xor_1 (xor_1_out, Cin, B);
  or or_1 (Cout, and_1_out, and_2_out, and_3_out);
  xor xor_2 (S, A, xor_1_out);
endmodule

module half_add (
  input  A,
  input  B,
  output S,
  output Cout
);

  xor xor_1 (S, A, B);
  and and_1 (Cout, B, A);
endmodule

module full_add_1_v2 (
  input  Cin,
  input  A,
  input  in_3,
  output S,
  output Cout
);

  wire half_add_1_cout, half_add_1_s, half_add_2_cout;

  half_add half_add_1 (.A(A), .B(in_3), .S(half_add_1_s), .Cout(half_add_1_cout));
  half_add half_add_2 (.A(Cin), .B(half_add_1_s), .S(S), .Cout(half_add_2_cout));
  half_add half_add_3 (.A(half_add_2_cout), .B(half_add_1_cout), .S(Cout));  // open: Cout
endmodule

module full_add_4 (
  input  Cin,
  input  [3:0] A,
  input  [3:0] B,
  output [3:0] S,
  output Cout
);

  wire full_add_1_1_cout, full_add_1_2_cout, full_add_1_3_cout;
  wire [7:0] sevenseghex_1_out_3;

  full_add_1 full_add_1_1 (.Cin(Cin), .A(A[0]), .B(B[0]), .S(S[0]), .Cout(full_add_1_1_cout));
  sevenSegHex sevenseghex_1 (.in_1(S), .hex_enable(1'b1), .out_3(sevenseghex_1_out_3));
  full_add_1 full_add_1_2 (.Cin(full_add_1_1_cout), .A(A[1]), .B(B[1]), .S(S[1]), .Cout(full_add_1_2_cout));
  _7_Segment_Display u_7_segment_display_1 (
    .g(sevenseghex_1_out_3[6]), .f(sevenseghex_1_out_3[5]), .a(sevenseghex_1_out_3[0]),
    .b(sevenseghex_1_out_3[1]), .e(sevenseghex_1_out_3[4]), .d(sevenseghex_1_out_3[3]),
    .c(sevenseghex_1_out_3[2]), .dp(sevenseghex_1_out_3[7]));
  full_add_1 full_add_1_3 (.Cin(full_add_1_2_cout), .A(A[2]), .B(B[2]), .S(S[2]), .Cout(full_add_1_3_cout));
  full_add_1 full_add_1_4 (.Cin(full_add_1_3_cout), .A(A[3]), .B(B[3]), .S(S[3]), .Cout(Cout));
endmodule

module four2pe (
  input  [3:0] in_1,
  output [1:0] out_2
);

  wire a0, a1, a2;

  and and_1 (a2, in_1[2], ~in_1[3]);  // AND_Gate
  and and_2 (a1, in_1[1], ~in_1[3], ~in_1[2]);  // AND_Gate
  and and_3 (a0, in_1[0], ~in_1[1], ~in_1[3], ~in_1[2]);  // AND_Gate
  or or_1 (out_2[0], a1, in_1[3]);
  or or_2 (out_2[1], a2, in_1[3]);

  // Other names for the same wires on the sheet: a3 = in_1[3]
endmodule

module four2pe2 (
  input  [3:0] in_1,
  output V,
  output [1:0] Y
);

  wire and_1_out;

  and and_1 (and_1_out, ~in_1[2], in_1[1]);  // AND_Gate
  or or_1 (Y[1], in_1[2], in_1[3]);
  or or_2 (Y[0], and_1_out, in_1[3]);
  or or_3 (V, in_1[0], in_1[1], in_1[2], in_1[3]);
endmodule

module sixteen4pe (
  output V,
  output [3:0] Y,
  output [7:0] groups
);

  wire [3:0] four2pe2_1_v;
  wire [7:0] sevenseghex_1_out_3;
  wire [15:0] dipswitch_1_p1;

  // DipSwitch #(.number(16)) dipswitch_1: pin names not known; wires that end beside it: dipswitch_1_p1[0], dipswitch_1_p1[1], dipswitch_1_p1[2], dipswitch_1_p1[3], dipswitch_1_p1[4], dipswitch_1_p1[5], dipswitch_1_p1[6], dipswitch_1_p1[7], dipswitch_1_p1[8], dipswitch_1_p1[9], dipswitch_1_p1[10], dipswitch_1_p1[11], dipswitch_1_p1[12], dipswitch_1_p1[13], dipswitch_1_p1[14], dipswitch_1_p1[15]
  four2pe2 four2pe2_1 (.in_1(dipswitch_1_p1[3:0]), .V(four2pe2_1_v[0]), .Y(groups[1:0]));
  four2pe2 four2pe2_2 (.in_1(dipswitch_1_p1[7:4]), .V(four2pe2_1_v[1]), .Y(groups[3:2]));
  four2pe2 four2pe2_3 (.in_1(dipswitch_1_p1[11:8]), .V(four2pe2_1_v[2]), .Y(groups[5:4]));
  four2pe2 four2pe2_4 (.in_1(dipswitch_1_p1[15:12]), .V(four2pe2_1_v[3]), .Y(groups[7:6]));
  BitSelector #(.group(2)) bitselector_1 (.in(groups), .out(Y[1:0]), .sel(Y[3:2]));
  four2pe2 four2pe2_5 (.in_1(four2pe2_1_v), .V(V), .Y(Y[3:2]));
  sevenSegHex sevenseghex_1 (.in_1(Y), .hex_enable(1'b1), .out_3(sevenseghex_1_out_3));
  _7_Segment_Display u_7_segment_display_1 (
    .g(sevenseghex_1_out_3[6]), .f(sevenseghex_1_out_3[5]), .a(sevenseghex_1_out_3[0]),
    .b(sevenseghex_1_out_3[1]), .e(sevenseghex_1_out_3[4]), .d(sevenseghex_1_out_3[3]),
    .c(sevenseghex_1_out_3[2]), .dp(sevenseghex_1_out_3[7]));
endmodule

module OneBitSub (
  input  A1,
  input  A0,
  input  Bin,
  output D,
  output Bout
);

  wire and_1_out, and_2_out, and_3_out, and_4_out, and_5_out;

  and and_1 (and_1_out, ~A1, ~A0, Bin);  // AND_Gate
  and and_2 (and_2_out, ~A1, A0, ~Bin);  // AND_Gate
  and and_3 (and_3_out, A1, ~A0, ~Bin);  // AND_Gate
  and and_4 (and_4_out, ~A1, A0, Bin);  // AND_Gate
  and and_5 (and_5_out, A1, A0, Bin);
  or or_1 (D, and_1_out, and_2_out, and_5_out, and_3_out);
  or or_2 (Bout, and_1_out, and_2_out, and_4_out, and_5_out);
endmodule

module full_sub_4 (
  input  Bin,
  input  [3:0] A1,
  input  [3:0] A0,
  output [3:0] D,
  output Bout
);

  wire onebitsub_1_bout, onebitsub_2_bout, onebitsub_3_bout;

  OneBitSub onebitsub_1 (.A1(A1[0]), .A0(A0[0]), .Bin(Bin), .D(D[0]), .Bout(onebitsub_1_bout));
  OneBitSub onebitsub_2 (.A1(A1[1]), .A0(A0[1]), .Bin(onebitsub_1_bout), .D(D[1]), .Bout(onebitsub_2_bout));
  OneBitSub onebitsub_3 (.A1(A1[2]), .A0(A0[2]), .Bin(onebitsub_2_bout), .D(D[2]), .Bout(onebitsub_3_bout));
  OneBitSub onebitsub_4 (.A1(A1[3]), .A0(A0[3]), .Bin(onebitsub_3_bout), .D(D[3]), .Bout(Bout));
endmodule

module OriginCode4Add (
  input  [3:0] A,
  input  [3:0] B,
  output [3:0] S
);

  wire FA, FB, full_sub_4_1_bout, not_1_out, xor_1_out;
  wire [1:0] bitselector_4_out, bitselector_5_out;
  wire [2:0] bitselector_1_out, bitselector_2_out;
  wire [3:0] full_add_4_1_s, full_sub_4_1_d, full_sub_4_2_d;
  wire [3:2] not_3_out;

  BitSelector #(.group(4)) bitselector_1 (.in({B, A}), .out({FA, bitselector_1_out}), .sel(A[3]));
  not not_1 (not_1_out, A[3]);
  BitSelector #(.group(4)) bitselector_2 (.in({B, A}), .out({FB, bitselector_2_out}), .sel(not_1_out));
  full_add_4 full_add_4_1 (
    .A({1'b0, bitselector_1_out}), .B({1'b0, bitselector_2_out}), .S(full_add_4_1_s));  // open: Cin, Cout
  full_sub_4 full_sub_4_1 (
    .A1({1'b0, bitselector_1_out}), .A0({1'b0, bitselector_2_out}), .D(full_sub_4_1_d),
    .Bout(full_sub_4_1_bout));  // open: Bin
  BitSelector #(.group(4), .width(16)) bitselector_3 (
    .in({1'b1, full_add_4_1_s[2:0], 1'b1, full_sub_4_2_d[2:0], 1'b0, full_sub_4_1_d[2:0], 1'b0, full_add_4_1_s[2:0]}),
    .out(S), .sel(bitselector_5_out));
  full_sub_4 full_sub_4_2 (
    .A1({1'b0, bitselector_2_out}), .A0({1'b0, bitselector_1_out}), .D(full_sub_4_2_d));  // open: Bin, Bout
  not not_2 (not_3_out[3], FA);
  not not_3 (not_3_out[2], FB);
  BitSelector #(.group(2), .width(4)) bitselector_4 (
    .in({not_3_out, FA, FB}), .out(bitselector_4_out), .sel(full_sub_4_1_bout));
  xor xor_1 (xor_1_out, FA, FB);
  BitSelector #(.group(2), .width(4)) bitselector_5 (
    .in({bitselector_4_out, FB, FA}), .out(bitselector_5_out), .sel(xor_1_out));
  // Probe on bitselector_5_out
endmodule

module onesComplement (
  input  [3:0] A,
  input  [3:0] B,
  output [3:0] out_3
);

  wire [2:0] origincode4add_1_s;
  wire [3:0] bitselector_1_out, bitselector_2_out, not_1_out, not_2_out, not_3_out, or_1_out, or_2_out;
  wire [3:3] origincode4add_1_s_2;

  assign not_1_out = ~A;  // NOT_Gate not_1, 4 bits wide
  assign not_2_out = ~B;  // NOT_Gate not_2, 4 bits wide
  assign or_1_out = 4'b1000 | not_1_out;  // OR_Gate or_1, 4 bits wide
  assign or_2_out = 4'b1000 | not_2_out;  // OR_Gate or_2, 4 bits wide
  BitSelector #(.group(4)) bitselector_1 (.in({or_1_out, A}), .out(bitselector_1_out), .sel(A[3]));
  BitSelector #(.group(4)) bitselector_2 (.in({or_2_out, B}), .out(bitselector_2_out), .sel(B[3]));
  // Probe on bitselector_1_out
  // Probe on bitselector_2_out
  OriginCode4Add origincode4add_1 (
    .A(bitselector_1_out), .B(bitselector_2_out), .S({origincode4add_1_s_2[3], origincode4add_1_s}));
  // Probe on {1'b0, origincode4add_1_s}
  assign not_3_out = ~{1'b0, origincode4add_1_s};  // NOT_Gate not_3, 4 bits wide
  BitSelector #(.group(4)) bitselector_3 (
    .in({not_3_out, origincode4add_1_s_2[3], origincode4add_1_s}), .out(out_3), .sel(origincode4add_1_s_2[3]));
endmodule

module twoscomplement (
  input  Cin,
  input  [3:0] A,
  input  [3:0] B,
  output [3:0] S,
  output Cout,
  output overflow
);

  wire and_1_out, and_2_out, full_add_1_1_cout, full_add_1_2_cout, full_add_1_3_cout;
  wire [7:0] sevenseghex_1_out_3;

  full_add_1 full_add_1_1 (.Cin(Cin), .A(A[0]), .B(B[0]), .S(S[0]), .Cout(full_add_1_1_cout));
  sevenSegHex sevenseghex_1 (.in_1(S), .hex_enable(1'b1), .out_3(sevenseghex_1_out_3));
  full_add_1 full_add_1_2 (.Cin(full_add_1_1_cout), .A(A[1]), .B(B[1]), .S(S[1]), .Cout(full_add_1_2_cout));
  _7_Segment_Display u_7_segment_display_1 (
    .g(sevenseghex_1_out_3[6]), .f(sevenseghex_1_out_3[5]), .a(sevenseghex_1_out_3[0]),
    .b(sevenseghex_1_out_3[1]), .e(sevenseghex_1_out_3[4]), .d(sevenseghex_1_out_3[3]),
    .c(sevenseghex_1_out_3[2]), .dp(sevenseghex_1_out_3[7]));
  full_add_1 full_add_1_3 (.Cin(full_add_1_2_cout), .A(A[2]), .B(B[2]), .S(S[2]), .Cout(full_add_1_3_cout));
  full_add_1 full_add_1_4 (.Cin(full_add_1_3_cout), .A(A[3]), .B(B[3]), .S(S[3]), .Cout(Cout));
  and and_1 (and_1_out, A[3], B[3], ~S[3]);  // AND_Gate
  and and_2 (and_2_out, ~A[3], ~B[3], S[3]);  // AND_Gate
  or or_1 (overflow, and_1_out, and_2_out);
endmodule

module SRLatch (
  input  R,
  input  in_2,
  input  S,
  output Q,
  output nQ
);

  wire and_1_out, and_2_out;

  and and_1 (and_1_out, R, in_2);
  and and_2 (and_2_out, in_2, S);
  nor nor_1 (Q, and_1_out, nQ);
  nor nor_2 (nQ, Q, and_2_out);
endmodule

module notSnotRLatch (
  input  R,
  input  S,
  output Q,
  output nQ
);

  nand nand_1 (Q, R, nQ);
  nand nand_2 (nQ, Q, S);
endmodule
